# Fritzing sketch sound-card-oscilliscope (saved by Fritzing 0.9.3b)
breadboards: 1

parts:
  R1 = Rotary Potentiometer (Small) [maximum_resistance=1MΩ package=THT]
  R2 = Rotary Potentiometer (Small) [maximum_resistance=1MΩ package=THT]
  LED1 = LED - 5mm [color="Green (555nm)" package="5 mm [THT]"]
  LED2 = LED - 5mm [color="Blue (470nm)" package="5 mm [THT]"]
  R3 = Resistor [tolerance=±5% resistance=4.7k package=THT]
  R4 = Resistor [tolerance=±5% resistance=4.7k package=THT]
  D1 = Diode [package=diode-1n4148]
  D2 = Diode [package=diode-1n4148]
  D4 = Diode [package=diode-1n4148]
  TRS1 = Audio Jack (TRS) 3.5mm [package="PG203J [THT]"]
  CLIP1 = Alligator Clip
  CLIP2 = Alligator Clip
  CLIP3 = Alligator Clip
  R5 = Resistor [tolerance=±5% resistance=470 package=THT]
  R6 = Resistor [tolerance=±5% resistance=470 package=THT]
  D3 = Diode [package=diode-1n4148]

nets:
  N1: R1.leg1, R2.leg2, D1.A, D2.A, D4.C, TRS1.Sleeve, CLIP1.wire, R5.Pin_0, R6.Pin_0, D3.C
  N2: R1.wiper, D1.C, TRS1.Ring
  N3: R1.leg2, R3.Pin_0
  N4: R2.leg1, R4.Pin_1
  N5: R2.wiper, D2.C, TRS1.Tip
  N6: LED1.cathode, R6.Pin_1
  N7: LED1.anode, R3.Pin_1, CLIP3.wire
  N8: LED2.cathode, R5.Pin_1
  N9: LED2.anode, R4.Pin_0, CLIP2.wire

custom parts:
  Alligator Clip: Alligator clip
  Alligator Clip: Alligator clip
  Alligator Clip: Alligator clip
